# Fritzing sketch led_pushbutton_buzzer (saved by Fritzing 0.9.3b)
breadboards: 1

parts:
  Part1 = Arduino Uno (Rev3)
  R1 = Resistor [tolerance=±5% resistance=10k package=THT]
  S1 = Pushbutton [package="[THT]"]
  J1 = Piezo Speaker

nets:
  N1: Part1.D7, R1.Pin_0, S1.Pin_1, S1.Pin_2
  N2: Part1.5V, S1.Pin_3, S1.Pin_4, J1.pin2
  N3: Part1.GND, R1.Pin_1, J1.pin1
