# Fritzing sketch obstacle _sensor (saved by Fritzing 0.9.3b)
circuit board: 8.46667cm x 5.64444cm
breadboards: 1

parts:
  Part1 = Arduino Uno (Rev3)
  OBSTACLE_SENSOR = QRD1114 [package=qrd1114]
  J1 = Piezo Speaker

nets:
  N1: Part1.D12/MISO, J1.pin2
  N2: Part1.D7, OBSTACLE_SENSOR.E
  N3: Part1.5V, OBSTACLE_SENSOR.C
  N4: Part1.GND, OBSTACLE_SENSOR.K, J1.pin1
