# Fritzing sketch pwm_led (saved by Fritzing 0.9.3b)
breadboards: 1

parts:
  Part1 = Arduino Uno (Rev3)
  LED1 = LED - 5mm [color="Red (633nm)" package="5 mm [THT]"]
  R2 = Rotary Potentiometer (Small) [maximum_resistance=100kΩ package=THT]
  R3 = Resistor [tolerance=±2% resistance=330 package=THT]

nets:
  N1: Part1.A0, R2.wiper
  N2: Part1.D12/MISO, R3.Pin_1
  N3: Part1.5V, R2.leg2
  N4: Part1.GND, LED1.cathode, R2.leg1
  N5: LED1.anode, R3.Pin_0
