# Fritzing sketch tone (saved by Fritzing 0.9.3b)
breadboards: 1

parts:
  Part1 = Arduino Uno (Rev3)
  C1 = Electrolytic Capacitor [capacitance=1µF package="100 mil [THT, electrolytic]"]
  J1 = Piezo Speaker

nets:
  N1: Part1.D8, C1.+
  N2: Part1.GND, J1.pin1
  N3: C1.-, J1.pin2
