# Fritzing sketch DC_voltmeter (saved by Fritzing 0.9.3b)
breadboards: 1

parts:
  Part1 = Arduino Uno (Rev3)
  R1-_LED_BACKLIGHT = Resistor [tolerance=±5% resistance=660 package=THT]
  LCD1 = LCD screen
  CONTRAST = POT [package=pot_alpha_rv16af-20]
  R1 = Resistor [tolerance=±5% resistance=11k package=THT]
  R2 = Resistor [tolerance=±5% resistance=2.2k package=THT]
  U1 = BATTERY-2 [package=battery-aa]

nets:
  N1: Part1.A0, R2.Pin_0
  N2: Part1.D11_PWM/MOSI, LCD1.E
  N3: Part1.D12/MISO, LCD1.RS
  N4: Part1.D2, LCD1.DB7
  N5: Part1.D3_PWM, LCD1.DB6
  N6: Part1.D4, LCD1.DB5
  N7: Part1.D5_PWM, LCD1.DB4
  5V: Part1.5V, R1-_LED_BACKLIGHT.Pin_1, LCD1.VDD, CONTRAST.A
  GND: Part1.GND, LCD1.VSS, LCD1.R/W, LCD1.LED-, CONTRAST.E, R2.Pin_1, U1.-1
  N8: R1-_LED_BACKLIGHT.Pin_0, LCD1.LED+
  N9: LCD1.V0, CONTRAST.S
  N10: R1.Pin_0, U1.+1
