# Fritzing sketch object_counter (saved by Fritzing 0.9.3b)
breadboards: 1

parts:
  Part1 = Arduino Uno (Rev3)
  R1-_LED_BACKLIGHT = Resistor [tolerance=±5% resistance=660 package=THT]
  LCD1 = LCD screen
  CONTRAST = POT [package=pot_alpha_rv16af-20]
  J1 = Piezo Speaker
  OBSTACLE_SENSOR = QRD1114 [package=qrd1114]

nets:
  N1: Part1.D11_PWM/MOSI, LCD1.E
  N2: Part1.D12/MISO, LCD1.RS
  N3: Part1.D13/SCK, J1.pin2
  N4: Part1.D2, LCD1.DB7
  N5: Part1.D3_PWM, LCD1.DB6
  N6: Part1.D4, LCD1.DB5
  N7: Part1.D5_PWM, LCD1.DB4
  N8: Part1.D7, OBSTACLE_SENSOR.E
  5V: Part1.5V, R1-_LED_BACKLIGHT.Pin_1, LCD1.VDD, CONTRAST.A, OBSTACLE_SENSOR.C
  GND: Part1.GND, LCD1.VSS, LCD1.R/W, LCD1.LED-, CONTRAST.E, J1.pin1, OBSTACLE_SENSOR.K
  N9: R1-_LED_BACKLIGHT.Pin_0, LCD1.LED+
  N10: LCD1.V0, CONTRAST.S
